# Fritzing sketch model (saved by Fritzing 0.9.3b)
breadboards: 1

parts:
  Part1 = Soil Moisture Sensor
  LED1 = RGB LED (com. anode, rbg) [package="5 mm [THT]"]
  Adafruit_HUZZAH_ESP8266_Breakout1 = Adafruit HUZZAH ESP8266 Breakout [part_number=2471]

nets:
  N1: Part1.SIG, Adafruit_HUZZAH_ESP8266_Breakout1.#2
  GND: Part1.GND, LED1.common_anode, Adafruit_HUZZAH_ESP8266_Breakout1.GND
  N2: Part1.VCC, Adafruit_HUZZAH_ESP8266_Breakout1.3V
  N3: LED1.red_cathode, Adafruit_HUZZAH_ESP8266_Breakout1.#0
  N4: LED1.blue_cathode, Adafruit_HUZZAH_ESP8266_Breakout1.#4
  N5: LED1.green_cathode, Adafruit_HUZZAH_ESP8266_Breakout1.#5
